// Logisim project CPU 4 bits CC4N LARA.circ as structural Verilog: 16 circuits, main circuit main
module main (
);

  wire clock_1_out, d_ff_1_q, d_ff_2_q, not_1_out, not_2_out, Reset_out, uc_1_ac, uc_1_d, uc_1_e, uc_1_ir,
       uc_1_load, uc_1_pc, uc_1_r_w, uc_1_ram, uc_1_reset_pc, ula_1_overflow, ula_1_zero;
  wire [2:0] uc_1_opcode;
  wire [3:0] ac_1_out_3, counter_1_q, mux_1_out_4, ram_1_data, \uc_1_endereço , uc_1_operando, ula_1_s;
  wire [7:0] ir_1_s, rom_1_data;

  not not_1 (not_1_out, uc_1_load);
  Counter #(.width(4), .max('hf), .trigger("falling")) counter_1 (
    .load(uc_1_load), .D(\uc_1_endereço ), .count(not_1_out), .Q(counter_1_q), .clk(uc_1_pc),
    .clr(uc_1_reset_pc));  // open: carry
  Clock clock_1 (.out(clock_1_out));
  Button Reset (.out(Reset_out));
  UC uc_1 (
    .\Instrução (ir_1_s), .Clock(clock_1_out), .Operando(uc_1_operando), .Z(d_ff_2_q),
    .\Endereço (\uc_1_endereço ), .Reset(Reset_out), .E(uc_1_e), .IR(uc_1_ir), .PC(uc_1_pc), .AC(uc_1_ac),
    .RAM(uc_1_ram), .Reset_PC(uc_1_reset_pc), .Opcode(uc_1_opcode), .O(d_ff_1_q), .Load(uc_1_load),
    .R_W(uc_1_r_w), .D(uc_1_d));
  // Probe on rom_1_data
  ROM #(.addrWidth(4)) rom_1 (.addr(counter_1_q), .data(rom_1_data));  // open: sel
  IR ir_1 (.Clock(uc_1_ir), .E(rom_1_data), .S(ir_1_s));
  // Probe on ir_1_s
  // Probe on ac_1_out_3
  // Probe on ula_1_s
  MUX mux_1 (.C(uc_1_e), .E(uc_1_operando), .D(ram_1_data), .out_4(mux_1_out_4));
  // Probe on mux_1_out_4
  ULA ula_1 (
    .D(uc_1_d), .B(mux_1_out_4), .A(ac_1_out_3), .in_4(uc_1_opcode), .Zero(ula_1_zero),
    .Overflow(ula_1_overflow), .S(ula_1_s));
  AC ac_1 (.out_3(ac_1_out_3), .in_1(uc_1_ac), .in_2(ula_1_s));
  RAM #(.addrWidth(4), .dataWidth(4)) ram_1 (
    .addr(uc_1_operando), .data(ram_1_data), .clk(uc_1_ram), .ld(uc_1_r_w));  // open: sel, clr
  not not_2 (not_2_out, uc_1_r_w);
  D_Flip_Flop d_ff_1 (.clk(uc_1_ac), .D(ula_1_overflow), .Q(d_ff_1_q));  // open: Qn, preset, en, reset
  D_Flip_Flop d_ff_2 (.clk(uc_1_ac), .D(ula_1_zero), .Q(d_ff_2_q));  // open: Qn, preset, en, reset
  Buffer_4 buffer_4_1 (.E(ac_1_out_3), .C(not_2_out), .S(ram_1_data));

  // Notes on the sheet:
  //   MOV
  //   0
  //   1
  //   MOV
  //   ADD
  //   2
  //   3
  //   ADD
  //   SUB
  //   4
  //   SUB
  //   5
  //   6
  //   OR
  //   OR
  //   7
  //   8
  //   NOT
  //   NOT
  //   9
  //   SHF
  //   A
  //   B
  //   SHF
  //   C
  //   JPZ
  //   JPO
  //   D
  //   GO
  //   E
  //   STR
  //   F
  //   Instruction Set
  //   0
  //   000
  //   AC <= X
  //   1
  //   000
  //   0
  //   001
  //   1
  //   001
  //   010
  //   0
  //   010
  //   1
  //   0
  //   011
  //   1
  //   011
  //   0
  //   100
  //   100
  //   1
  //   101
  //   0
  //   1
  //   101
  //   0
  //   110
  //   1
  //   110
  //   PC <= X
  //   111
  //   0
  //   1
  //   111
  //   AC <= M(X)
  //   AC <= AC+X
  //   AC <= AC+M(X)
  //   AC <= AC-X
  //   AC <= AC-M(X)
  //   AC <= AC OR X
  //   AC <= AC OR M(X)
  //   AC <= NOT X
  //   AC <= NOT M( X)
  //   AC <= AC << Q
  //   AC <= AC >> Q
  //   PC <= X SE FLAG Z
  //   PC <= X SE FLAG O
  //   M(X) <= AC 
  //   Memória do Programa
  //   PROCESSADOR RISC 4 BITS - LARA MIRANDA FERNANDES - CC4N
  //   contents of rom_1 (hex, n*v repeats v):
  //   0 f0 1 f1 10 31 d0 f2 11 f0 12 f1 e4
  //   Memória de Dados
endmodule

module ADD_1 (
  input  A,
  input  B,
  input  C,
  output S,
  output Vai_1
);

  wire and_1_out, and_2_out, or_1_out, xor_1_out;

  or or_1 (or_1_out, C, B);
  xor xor_1 (xor_1_out, C, B);
  and and_1 (and_1_out, or_1_out, A);
  and and_2 (and_2_out, C, B);
  xor xor_2 (S, xor_1_out, A);
  or or_2 (Vai_1, and_1_out, and_2_out);
endmodule

module Add_4 (
  input  [3:0] B,
  input  [3:0] A,
  output Overflow,
  output [3:0] S
);

  wire add_1_2_vai_1, add_1_3_vai_1, add_1_4_vai_1;

  ADD_1 add_1_1 (.S(S[3]), .Vai_1(Overflow), .A(A[3]), .B(B[3]), .C(add_1_2_vai_1));
  ADD_1 add_1_2 (.S(S[2]), .Vai_1(add_1_2_vai_1), .A(A[2]), .B(B[2]), .C(add_1_3_vai_1));
  ADD_1 add_1_3 (.S(S[1]), .Vai_1(add_1_3_vai_1), .A(A[1]), .B(B[1]), .C(add_1_4_vai_1));
  ADD_1 add_1_4 (.S(S[0]), .Vai_1(add_1_4_vai_1), .A(A[0]), .B(B[0]), .C(1'b0));
endmodule

module Sub_1 (
  input  A,
  input  B,
  input  VEM_1,
  output S,
  output Vai_1
);

  wire and_1_out, and_2_out, or_1_out, xor_1_out;

  or or_1 (or_1_out, B, VEM_1);
  xor xor_1 (xor_1_out, A, B);
  and and_1 (and_1_out, or_1_out, ~A);  // AND_Gate
  and and_2 (and_2_out, VEM_1, B);
  xor xor_2 (S, xor_1_out, VEM_1);
  or or_2 (Vai_1, and_1_out, and_2_out);
endmodule

module Sub_4 (
  input  [3:0] B,
  input  [3:0] A,
  output Overflow,
  output [3:0] S
);

  wire sub_1_2_vai_1, sub_1_3_vai_1, sub_1_4_vai_1;

  // Probe on A
  Sub_1 sub_1_1 (.S(S[3]), .Vai_1(Overflow), .A(A[3]), .B(B[3]), .VEM_1(sub_1_2_vai_1));
  Sub_1 sub_1_2 (.S(S[2]), .Vai_1(sub_1_2_vai_1), .A(A[2]), .B(B[2]), .VEM_1(sub_1_3_vai_1));
  Sub_1 sub_1_3 (.S(S[1]), .Vai_1(sub_1_3_vai_1), .A(A[1]), .B(B[1]), .VEM_1(sub_1_4_vai_1));
  // Probe on S
  Sub_1 sub_1_4 (.S(S[0]), .Vai_1(sub_1_4_vai_1), .A(A[0]), .B(B[0]), .VEM_1(1'b0));
  // Probe on B
endmodule

module Rot_Esq (
  input  [3:0] a_b_c_d,
  input  [1:0] x_y,
  output [3:0] A_B_C_D_2
);

  wire and_1_out, and_2_out, and_3_out, and_4_out, and_5_out, and_6_out, and_7_out, and_8_out, and_9_out;

  and and_1 (and_1_out, ~x_y[1], ~x_y[0], a_b_c_d[3]);  // AND_Gate
  and and_2 (and_2_out, ~x_y[1], x_y[0], a_b_c_d[2]);  // AND_Gate
  and and_3 (and_3_out, x_y[1], ~x_y[0], a_b_c_d[1]);  // AND_Gate
  and and_4 (and_4_out, x_y[1], x_y[0], a_b_c_d[0]);
  and and_5 (and_5_out, ~x_y[1], ~x_y[0], a_b_c_d[2]);  // AND_Gate
  and and_6 (and_6_out, ~x_y[1], x_y[0], a_b_c_d[1]);  // AND_Gate
  and and_7 (and_7_out, x_y[1], ~x_y[0], a_b_c_d[0]);  // AND_Gate
  and and_8 (and_8_out, ~x_y[1], ~x_y[0], a_b_c_d[1]);  // AND_Gate
  and and_9 (and_9_out, ~x_y[1], x_y[0], a_b_c_d[0]);  // AND_Gate
  and and_10 (A_B_C_D_2[0], ~x_y[1], ~x_y[0], a_b_c_d[0]);  // AND_Gate
  or or_1 (A_B_C_D_2[3], and_1_out, and_2_out, and_3_out, and_4_out);
  or or_2 (A_B_C_D_2[2], and_5_out, and_6_out, and_7_out);
  or or_3 (A_B_C_D_2[1], and_8_out, and_9_out);
endmodule

module Rot_Dir (
  input  [3:0] a_b_c_d,
  input  [1:0] x_y,
  output [3:0] A_B_C_D_2
);

  wire and_1_out, and_2_out, and_3_out, and_4_out, and_5_out, and_6_out, and_7_out, and_8_out, and_9_out;

  and and_1 (and_1_out, ~x_y[1], ~x_y[0], a_b_c_d[0]);  // AND_Gate
  and and_2 (and_2_out, ~x_y[1], x_y[0], a_b_c_d[1]);  // AND_Gate
  and and_3 (and_3_out, x_y[1], ~x_y[0], a_b_c_d[2]);  // AND_Gate
  and and_4 (and_4_out, x_y[1], x_y[0], a_b_c_d[3]);
  and and_5 (and_5_out, ~x_y[1], ~x_y[0], a_b_c_d[1]);  // AND_Gate
  and and_6 (and_6_out, ~x_y[1], x_y[0], a_b_c_d[2]);  // AND_Gate
  and and_7 (and_7_out, x_y[1], ~x_y[0], a_b_c_d[3]);  // AND_Gate
  and and_8 (and_8_out, ~x_y[1], ~x_y[0], a_b_c_d[2]);  // AND_Gate
  and and_9 (and_9_out, ~x_y[1], x_y[0], a_b_c_d[3]);  // AND_Gate
  and and_10 (A_B_C_D_2[3], ~x_y[1], ~x_y[0], a_b_c_d[3]);  // AND_Gate
  or or_1 (A_B_C_D_2[0], and_1_out, and_2_out, and_3_out, and_4_out);
  or or_2 (A_B_C_D_2[1], and_5_out, and_6_out, and_7_out);
  or or_3 (A_B_C_D_2[2], and_8_out, and_9_out);
endmodule

module DECODIFI (
  input  [2:0] in_1,
  output S0,
  output S1,
  output S2,
  output S3,
  output S4,
  output S5,
  output S6,
  output S7
);

  wire not_1_out, not_2_out, not_3_out, not_4_out, not_5_out, not_6_out, not_7_out, not_8_out, not_9_out,
       not_10_out, not_11_out, not_12_out;

  not not_1 (not_1_out, in_1[2]);
  not not_2 (not_2_out, in_1[1]);
  not not_3 (not_3_out, in_1[0]);
  not not_4 (not_4_out, in_1[2]);
  not not_5 (not_5_out, in_1[1]);
  not not_6 (not_6_out, in_1[2]);
  not not_7 (not_7_out, in_1[0]);
  not not_8 (not_8_out, in_1[2]);
  not not_9 (not_9_out, in_1[1]);
  not not_10 (not_10_out, in_1[0]);
  not not_11 (not_11_out, in_1[1]);
  not not_12 (not_12_out, in_1[0]);
  and and_1 (S7, in_1[2], in_1[1], in_1[0]);
  and and_2 (S0, not_1_out, not_2_out, not_3_out);
  and and_3 (S1, not_4_out, not_5_out, in_1[0]);
  and and_4 (S2, not_6_out, in_1[1], not_7_out);
  and and_5 (S3, not_8_out, in_1[1], in_1[0]);
  and and_6 (S4, in_1[2], not_9_out, not_10_out);
  and and_7 (S5, in_1[2], not_11_out, in_1[0]);
  and and_8 (S6, in_1[2], in_1[1], not_12_out);
endmodule

module Buffer_4 (
  input  [3:0] E,
  input  C,
  output [3:0] S
);

  assign S[3] = C ? E[3] : 1'bz;  // Controlled_Buffer controlled_buffer_1
  assign S[0] = C ? E[0] : 1'bz;  // Controlled_Buffer controlled_buffer_2
  assign S[1] = C ? E[1] : 1'bz;  // Controlled_Buffer controlled_buffer_3
  assign S[2] = C ? E[2] : 1'bz;  // Controlled_Buffer controlled_buffer_4
endmodule

module OR (
  input  [3:0] B,
  input  [3:0] A,
  output [3:0] S
);

  or or_1 (S[3], A[3], B[3]);
  or or_2 (S[2], A[2], B[2]);
  or or_3 (S[1], A[1], B[1]);
  or or_4 (S[0], A[0], B[0]);
endmodule

module Not (
  input  [3:0] E,
  output [3:0] S
);

  not not_1 (S[3], E[3]);
  not not_2 (S[1], E[1]);
  not not_3 (S[2], E[2]);
  not not_4 (S[0], E[0]);
endmodule

module ULA (
  input  D,
  input  [3:0] B,
  input  [3:0] A,
  input  [2:0] in_4,
  output Overflow,
  output [3:0] S,
  output Zero
);

  wire add_4_1_overflow, and_1_out, and_2_out, decodifi_1_s0, decodifi_1_s1, decodifi_1_s2, decodifi_1_s3,
       decodifi_1_s4, decodifi_1_s5, decodifi_1_s6, decodifi_1_s7, not_2_out, sub_4_1_overflow;
  wire [3:0] add_4_1_s, buffer_4_6_s, not_1_s, or_2_s, rot_dir_1_a_b_c_d_2, rot_esq_1_a_b_c_d_2, sub_4_1_s;

  or or_1 (Overflow, and_1_out, and_2_out);
  and and_1 (and_1_out, add_4_1_overflow, decodifi_1_s1);
  and and_2 (and_2_out, sub_4_1_overflow, decodifi_1_s2);
  DECODIFI decodifi_1 (
    .in_1(in_4), .S0(decodifi_1_s0), .S1(decodifi_1_s1), .S2(decodifi_1_s2), .S3(decodifi_1_s3),
    .S4(decodifi_1_s4), .S5(decodifi_1_s5), .S6(decodifi_1_s6), .S7(decodifi_1_s7));
  Buffer_4 buffer_4_1 (.E(B), .C(decodifi_1_s0), .S(S));
  Add_4 add_4_1 (.A(A), .Overflow(add_4_1_overflow), .B(B), .S(add_4_1_s));
  Buffer_4 buffer_4_2 (.E(add_4_1_s), .C(decodifi_1_s1), .S(S));
  Sub_4 sub_4_1 (.A(A), .Overflow(sub_4_1_overflow), .B(B), .S(sub_4_1_s));
  Buffer_4 buffer_4_3 (.E(sub_4_1_s), .C(decodifi_1_s2), .S(S));
  nor nor_1 (Zero, S[0], S[1], S[2], S[3], decodifi_1_s6, decodifi_1_s7);
  Not not_1 (.E(B), .S(not_1_s));
  OR or_2 (.A(A), .B(B), .S(or_2_s));
  Buffer_4 buffer_4_4 (.E(not_1_s), .C(decodifi_1_s4), .S(S));
  Buffer_4 buffer_4_5 (.E(or_2_s), .C(decodifi_1_s3), .S(S));
  // Probe on S
  Rot_Esq rot_esq_1 (.a_b_c_d(A), .x_y(B[1:0]), .A_B_C_D_2(rot_esq_1_a_b_c_d_2));
  Rot_Dir rot_dir_1 (.a_b_c_d(A), .x_y(B[1:0]), .A_B_C_D_2(rot_dir_1_a_b_c_d_2));
  Buffer_4 buffer_4_6 (.E(rot_esq_1_a_b_c_d_2), .C(not_2_out), .S(buffer_4_6_s));
  not not_2 (not_2_out, D);
  Buffer_4 buffer_4_7 (.E(rot_dir_1_a_b_c_d_2), .C(D), .S(buffer_4_6_s));
  Buffer_4 buffer_4_8 (.E(buffer_4_6_s), .C(decodifi_1_s5), .S(S));
endmodule

module AC (
  input  in_1,
  input  [3:0] in_2,
  output [3:0] out_3
);

  D_Flip_Flop d_ff_1 (.clk(in_1), .D(in_2[3]), .Q(out_3[3]));  // open: Qn, preset, en, reset
  D_Flip_Flop d_ff_2 (.clk(in_1), .D(in_2[2]), .Q(out_3[2]));  // open: Qn, preset, en, reset
  D_Flip_Flop d_ff_3 (.clk(in_1), .D(in_2[1]), .Q(out_3[1]));  // open: Qn, preset, en, reset
  D_Flip_Flop d_ff_4 (.clk(in_1), .D(in_2[0]), .Q(out_3[0]));  // open: Qn, preset, en, reset
endmodule

module MUX (
  input  [3:0] E,
  input  [3:0] D,
  input  C,
  output [3:0] out_4
);

  wire not_1_out;

  Buffer_4 buffer_4_1 (.E(E), .C(not_1_out), .S(out_4));
  not not_1 (not_1_out, C);
  Buffer_4 buffer_4_2 (.E(D), .C(C), .S(out_4));
endmodule

module IR (
  input  Clock,
  input  [7:0] E,
  output [7:0] S
);

  D_Flip_Flop #(.trigger("falling")) D7 (.clk(Clock), .D(E[7]), .Q(S[7]));  // open: Qn, preset, en, reset
  D_Flip_Flop #(.trigger("falling")) D6 (.clk(Clock), .D(E[6]), .Q(S[6]));  // open: Qn, preset, en, reset
  D_Flip_Flop #(.trigger("falling")) D5 (.clk(Clock), .D(E[5]), .Q(S[5]));  // open: Qn, preset, en, reset
  D_Flip_Flop #(.trigger("falling")) D4 (.clk(Clock), .D(E[4]), .Q(S[4]));  // open: Qn, preset, en, reset
  D_Flip_Flop #(.trigger("falling")) D3 (.clk(Clock), .D(E[3]), .Q(S[3]));  // open: Qn, preset, en, reset
  D_Flip_Flop #(.trigger("falling")) D2 (.clk(Clock), .D(E[2]), .Q(S[2]));  // open: Qn, preset, en, reset
  D_Flip_Flop #(.trigger("falling")) D1 (.clk(Clock), .D(E[1]), .Q(S[1]));  // open: Qn, preset, en, reset
  D_Flip_Flop #(.trigger("falling")) D0 (.clk(Clock), .D(E[0]), .Q(S[0]));  // open: Qn, preset, en, reset
endmodule

module UC (
  input  [7:0] \Instrução ,
  input  Clock,
  input  Z,
  input  Reset,
  input  O,
  output [3:0] Operando,
  output [3:0] \Endereço ,
  output IR,
  output PC,
  output AC,
  output RAM,
  output Reset_PC,
  output D,
  output E,
  output [2:0] Opcode,
  output Load,
  output R_W
);

  wire GOTO_out, JPO_out, JPZ_out, nand_1_out, R_1_W_0_out;
  wire [1:0] counter_1_q;

  Counter #(.width(2), .max('h3)) counter_1 (.Q(counter_1_q), .clk(Clock), .clr(Reset));  // open: load, D, count, carry
  and R_1_W_0 (R_1_W_0_out, AC, \Instrução [7], \Instrução [6], \Instrução [5], \Instrução [4]);
  not not_1 (R_W, R_1_W_0_out);
  and u_IR (IR, ~counter_1_q[1], ~counter_1_q[0]);  // AND_Gate
  and u_AC (AC, counter_1_q[1], ~counter_1_q[0]);  // AND_Gate
  and u_PC (PC, ~counter_1_q[1], counter_1_q[0]);  // AND_Gate
  and JPO (JPO_out, \Instrução [7], \Instrução [6], ~\Instrução [5], \Instrução [4], PC, O);  // AND_Gate
  and u_RAM (RAM, counter_1_q[1], counter_1_q[0]);
  and JPZ (JPZ_out, \Instrução [7], \Instrução [6], ~\Instrução [5], ~\Instrução [4], Z, PC);  // AND_Gate
  and GOTO (GOTO_out, PC, \Instrução [7], \Instrução [6], \Instrução [5], ~\Instrução [4]);  // AND_Gate
  or or_1 (Load, GOTO_out, JPZ_out, JPO_out);
  nand nand_1 (nand_1_out, \Instrução [7], ~\Instrução [6], \Instrução [5]);  // NAND_Gate
  and and_1 (E, \Instrução [4], nand_1_out);

  assign D = \Instrução [4];
  assign \Endereço  = \Instrução [3:0];
  assign Opcode = \Instrução [7:5];
  assign Operando = \Instrução [3:0];
  assign Reset_PC = Reset;
endmodule
